# Fritzing sketch led-clock (saved by Fritzing 0.9.5d)

parts:
  Part1 = Matrix LED de 8x8 basada en MAX7219
  Part2 = Matrix LED de 8x8 basada en MAX7219
  Part3 = Matrix LED de 8x8 basada en MAX7219
  Part4 = Matrix LED de 8x8 basada en MAX7219
  ZS-042_RTC1 = ZS-042 RTC Module
  LoRa_Module1 = Ra-01 - LoRa Module SX1278 [part_number=SX1278]
  U1 = LuaNode32 / ESP32 [part_number=ESP32S-PIN30]
  Part5 = BH1750

nets:
  N1: Part1.CS, U1.D5
  N2: Part1.CLK, U1.D18
  N3: Part1.DIN, U1.D23
  N4: Part1.VCC(OUT), Part2.VCC
  N5: Part1.GND#6, Part2.GND#1
  N6: Part1.CS(OUT), Part2.CS
  N7: Part1.CLK(OUT), Part2.CLK
  N8: Part1.DOUT, Part2.DIN
  N9: Part2.VCC(OUT), Part3.VCC
  N10: Part2.GND#6, Part3.GND#1
  N11: Part2.CS(OUT), Part3.CS
  N12: Part2.CLK(OUT), Part3.CLK
  N13: Part2.DOUT, Part3.DIN
  N14: Part3.VCC(OUT), Part4.VCC
  N15: Part3.GND#6, Part4.GND
  N16: Part3.CS(OUT), Part4.CS
  N17: Part3.CLK(OUT), Part4.CLK
  N18: Part3.DOUT, Part4.DIN
  GND: ZS-042_RTC1.GND, U1.GND
  VCC: ZS-042_RTC1.VCC, U1.3V3
  N19: ZS-042_RTC1.SDA, U1.D21
  N20: ZS-042_RTC1.SCL, U1.D22
  N21: LoRa_Module1.NSS, U1.D15
  N22: LoRa_Module1.MOSI, U1.D13
  N23: LoRa_Module1.MISO, U1.D12
  N24: LoRa_Module1.SCK, U1.D14
  N25: LoRa_Module1.RESET, U1.D27
  N26: LoRa_Module1.DIO0, U1.D26
  N27: U1.D32, Part5.SCL
  N28: U1.D33, Part5.SDA

notes:
  3.3V
  GND
  LED-CLOCK v1.0 by luk6xff

custom parts:
  Ra-01 - LoRa Module SX1278: The Ra-01 LoRa Module featuring the SX1278 engine by Semtech. Module by AI-Thinker. Module (Ra-01) specifications from: https://www.banggood.com/Ra-01-Smart-Electronics-SX1278-LoRa-Spread-Spectrum-Wireless-Module-Ultra-Far-10KM-433M-p-1130769.html Description: Power supply: DC1.8-3.7V(3.3V) Chip: SX1278 Frequency: 433Mhz Operating temperature: -40~+85°C On Sheild Description (may vary by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
  LuaNode32 / ESP32: New Image for LuaNode32 DOIT ESP32 DEVKIT V1. Base parts from LuaNode32 / ESP32 ESP32 based LuaNode32 by G.Noorlander DOIT Esp32 DevKit v1 (30 pins long, 11 pins width) by Werner Rothschopf (modified by vanepp Dec 2018)
  BH1750: Light Sensor
